# Fritzing sketch TonUINO (saved by Fritzing 0.9.3b)
breadboards: 1

parts:
  part = DFPlayer MINI [package="DIP (Dual Inline) [THT]"]
  part_2 = Arduino Nano (Rev3.0)
  part_3 = Resistor [tolerance=±5% resistance=1k package=THT]
  part_4 = Loudspeaker
  Vol_+ = Pushbutton [package="[THT]"]
  Vol_- = Pushbutton [package="[THT]"]
  Play/Pause = Pushbutton [package="[THT]"]
  Up = Pushbutton [package="[THT]"]
  Down = Pushbutton [package="[THT]"]
  part_5 = RFID-RC522-v3

nets:
  VCC: part.VCC, part_2.5V
  N1: part.RX, part_3.Pin_0
  N2: part.TX, part_2.D2
  N3: part.SPK1, part_4.pin2
  N4: part.SPK2, part_4.pin1
  GND: part.GND, part_2.GND, Vol_+.Pin_1, Vol_+.Pin_2, Vol_-.Pin_1, Vol_-.Pin_2, Play/Pause.Pin_1, Play/Pause.Pin_2, Up.Pin_1, Up.Pin_2, Down.Pin_1, Down.Pin_2
  N5: part.BUSY, part_2.D4
  N6: part_2.D3, part_3.Pin_1
  N7: part_2.D9, part_5.GND
  N8: part_2.D10, part_5.SDA
  N9: part_2.D11/MOSI, part_5.MOSI
  N10: part_2.D12/MISO, part_5.MISO
  N11: part_2.A4, Vol_+.Pin_3, Vol_+.Pin_4
  N12: part_2.A3, Vol_-.Pin_4
  N13: part_2.A2, Down.Pin_3, Down.Pin_4
  N14: part_2.A1, Up.Pin_4
  N15: part_2.A0, Play/Pause.Pin_4
  3V3: part_2.3V3, part_5.3.3V
  N16: part_2.D13/SCK, part_5.SCK

custom parts:
  DFPlayer MINI: MP3 module by DFRobot.com for playing Music from an SD-Card. Supports WAV and MP3 files.
  RFID-RC522-v3: A simple China made RFID-RC522 Reader (6x4 cm); do check the pin labels, as this is a MFRC522 based clone.
